# Fritzing sketch theDudeTemp (saved by Fritzing 0.9.2b)

parts:
  R2 = Resistor [tolerance=±5% resistance=10k package=THT]
  R1 = Resistor [tolerance=±5% resistance=5.6k package=THT]
  C1 = Electrolytic Capacitor [capacitance=2.2µF package="100 mil [THT, electrolytic]"]
  U2 = ESP8266 WiFi Module [part_number=ESP8266]
  R4 = Temperature Sensor (Thermistor) [thermistor_type=NTC package=THT]
  U3 = V_REG MIC5219 [package=sot23-5]
  U4 = LIPO-110mAh [package=lipo-110]
  Part1 = USB LiPoly Charger
  C4 = Capacitor [package=cap-pth-small2]
  D2 = SOLAR-IXYS [package=solarbit-12x1]  # not connected
  R5 = Resistor [tolerance=±5% resistance=1k package=THT]
  R6 = Resistor [tolerance=±5% resistance=10k package=THT]
  R7 = Resistor [tolerance=±5% resistance=10k package=THT]
  C5 = Electrolytic Capacitor [capacitance=2.2µF package="100 mil [THT, electrolytic]"]
  R8 = Resistor [tolerance=±5% resistance=10k package=THT]
  S1 = Pushbutton [package="[THT]"]
  S2 = Pushbutton [package="[THT]"]

nets:
  GND: R2.Pin_0, C1.-, U2.GND, U2.IO15, U3.GND, U4.-, Part1.GND, C4.1, R5.Pin_0, R5.Pin_1, C5.-, S1.Pin_3, S1.Pin_4, S2.Pin_3, S2.Pin_4
  N1: R2.Pin_1, R1.Pin_1, U3.BP, C4.2
  N2: R1.Pin_0, C1.+, U2.3.3V, U2.CHIP_EN, R4.pin_1, U3.OUT, R6.Pin_1, R7.Pin_0, R8.Pin_0
  N3: U2.IO0, R7.Pin_1, S1.Pin_1
  N4: U2.IO2, R8.Pin_1
  N5: U2.T_OUT, R4.pin_0
  N6: U2.RST, U2.XPD, R6.Pin_0, C5.+, S2.Pin_2
  N7: U3.IN, U3.EN, U4.+, Part1.VBAT

notes:
  Solar Cell - 5V, 250mA
  650mA, 3.7V
  2.2uF
  470pF
  10K
  5.6K
  CH_PD/EN
  ADC
  1K
  TDC310
  RST
  100nF
  RESET
  FLASH
  IO0
  IO2
  IO15
  Exposed
  Hidden
  3.3V
